# Fritzing sketch Sreesat_Measurement_Sensors (saved by Fritzing 0.9.3b)

parts:
  GPS1 = Adafruit Ultimate GPS Breakout
  Part1 = Arduino Uno (Rev3) - ICSP
  Grove1 = Grove Button
  Part2 = BME280 Breakout

nets:
  N1: GPS1.TX, Part1.D3_PWM
  N2: GPS1.RX, Part1.D4
  GND: GPS1.GND, Part1.GND
  VIN: GPS1.VIN, Part1.5V
  N3: Part1.A4/SDA, Grove1.SIG
  N4: Part1.A5/SCL, Grove1.NC
  3V3: Part1.3V3, Part2.3.3V

notes:
  SDA,SCL,Vcc,GND
  SCl,SDA,Vcc,GND
  Tx,Rx,GND,Vin
